# Fritzing sketch 002 (saved by Fritzing 1.0.6)
breadboards: 1

parts:
  Part1 = Arduino Mega 2560 (Rev3)
  GLCD_128x1 = 128 x 64 Graphic LCD
  R1 = Resistor [tolerance=±5% power=0.25W resistance=220 package=THT]
  R2 = Resistor [tolerance=±5% power=0.25W resistance=220 package=THT]
  R3 = 6mm Trimmer Potentiometer [maximum_resistance=10kΩ knob_status=25% power=0.5W package=THT]
  J3 = Camdenboss CTB0158-3 [part_number=CTB0158-3 package=THT]
  J1 = Camdenboss CTB0158-5 [part_number=CTB0158-5 package=THT]
  U1 = 555 Timer [package="DIP8 [THT]"]
  J4 = Camdenboss CTB0158-3 [part_number=CTB0158-3 package=THT]

nets:
  N1: Part1.5V, GLCD_128x1.2_Vdd, GLCD_128x1.19_A(+)
  N2: Part1.GND, GLCD_128x1.1_Vss, GLCD_128x1.20_K(-), R3.leg1, J3.pin1, J1.pin1, U1.Threshold, U1.Vcc_Supply_Voltage
  N3: Part1.D2_PWM, J1.pin5
  N4: Part1.D3_PWM, J1.pin4
  N5: Part1.D4_PWM, J1.pin3
  N6: Part1.D5_PWM, J1.pin2
  N7: Part1.D6_PWM, J3.pin3
  N8: Part1.D7_PWM, J3.pin2
  N9: Part1.D22, GLCD_128x1.4_D/I
  N10: Part1.D23, GLCD_128x1.5_R/W
  N11: Part1.D24, GLCD_128x1.6_Enable
  N12: Part1.D25, GLCD_128x1.7_DB0
  N13: Part1.D26, GLCD_128x1.8_DB1
  N14: Part1.D27, GLCD_128x1.9_BD2
  N15: Part1.D28, GLCD_128x1.10_DB3
  N16: Part1.D29, GLCD_128x1.11_DB4
  N17: Part1.D30, GLCD_128x1.12_DB5
  N18: Part1.D31, GLCD_128x1.13_DB6
  N19: Part1.D32, GLCD_128x1.14_DB7
  N20: Part1.D33, GLCD_128x1.15_CS1
  N21: Part1.D34, GLCD_128x1.16_CS2
  N22: Part1.D35, GLCD_128x1.17_RST
  N23: Part1.D42, R1.Pin_1
  N24: Part1.D44, R2.Pin_1
  N25: GLCD_128x1.3_Vo, R3.leg2
  N26: GLCD_128x1.18_Vout, R3.wiper
  N27: R1.Pin_0, U1.Control_Voltage
  N28: R2.Pin_0, U1.Discharge
  N29: U1.Ground, U1.Output, J4.pin1
  N30: U1.Trigger, J4.pin2
  N31: U1.Reset, J4.pin3
